# Fritzing sketch Arduino Uno + Screen + Encoder Demo (saved by Fritzing 0.9.3b)
breadboards: 1

parts:
  Part1 = Arduino Uno (Rev3)
  IC1 = IC, SIP package, 5 pins [chip_label=Encoder]
  IC2 = IC, SIP package, 4 pins [chip_label="SCREEN PINS"]
  R2 = Resistor [tolerance=±5% resistance=4.7k package=THT]
  R1 = Resistor [tolerance=±5% resistance=4.7k package=THT]

nets:
  N1: Part1.A4/SDA, IC2.pin4, R2.Pin_1
  N2: Part1.A5/SCL, IC2.pin3, R1.Pin_1
  N3: Part1.D5_PWM, IC1.pin1
  N4: Part1.D6_PWM, IC1.pin2
  N5: Part1.D7, IC1.pin3
  N6: Part1.3V3, IC2.pin2, R2.Pin_0, R1.Pin_0
  N7: Part1.5V, IC1.pin4
  N8: Part1.GND, IC1.pin5, IC2.pin1
